// Logisim project 25CSB1A27_SingireddyTrinadhReddy_COA.circ as structural Verilog: 12 circuits, main circuit main
module main (
  input  pin_bit0,
  input  pin_bit1,
  input  pin_bit2,
  input  pin_bit3,
  input  Reset_btn,
  output VOTEAccepted_A,
  output VOTEAccepted_B,
  output Blocked,
  output VOTEAccepted_C,
  output [3:0] Anyvote_clk,
  output Any_Vote,
  output VOTEAccepted_D,
  output PIN_Match,
  output Admin_out,
  output EnableSet_out,
  output Locked_out,
  output [3:0] Wrong_count
);

  wire and_2_out, and_3_out, and_4_out, CandidateA_btn_out, CandidateB_btn_out, CandidateC_btn_out,
       CandidateD_btn_out, comparator_1_eq, comparator_2_gt, EnableSet_And_out, NOR_Q_out, NOR_Qp_out,
       not_1_out, not_2_out, not_3_out, or_1_out, OR_1_out_2, or_2_out, OR_2_out_2, or_3_out, or_4_out,
       xnor_1_out, xnor_2_out, xnor_3_out, xnor_4_out;
  wire [3:0] adder_1_out, adder_2_out, adder_3_out, counter_2_q, counter_3_q, counter_4_q, counter_5_q;

  or or_1 (or_1_out, CandidateA_btn_out, CandidateB_btn_out);
  or or_2 (or_2_out, or_1_out, CandidateC_btn_out);
  or or_3 (or_3_out, or_2_out, CandidateD_btn_out);
  D_Flip_Flop d_ff_1 (.D(1'b1), .clk(or_3_out), .Q(Blocked), .preset(1'b0), .reset(NOR_Q_out));  // open: Qn
  LED led_1 (.in(Blocked));
  xnor xnor_1 (xnor_1_out, pin_bit0, 1'b1);
  xnor xnor_2 (xnor_2_out, pin_bit1, 1'b0);
  xnor xnor_3 (xnor_3_out, pin_bit2, 1'b1);
  xnor xnor_4 (xnor_4_out, pin_bit3, 1'b1);
  not not_1 (not_1_out, PIN_Match);
  and and_1 (EnableSet_out, EnableSet_And_out, not_2_out);
  Button CandidateA_btn (.out(CandidateA_btn_out));
  and and_2 (and_2_out, xnor_1_out, xnor_2_out);
  and and_3 (and_3_out, xnor_3_out, xnor_4_out);
  and and_4 (and_4_out, not_1_out, Admin_out);
  Counter #(.max('h3), .ongoal("stay"), .width(4)) counter_1 (
    .clr(or_4_out), .load(1'b0), .up(1'b1), .count(1'b1), .clk(and_4_out), .D(4'b0000), .carry(Locked_out),
    .Q(Wrong_count));
  Button CandidateB_btn (.out(CandidateB_btn_out));
  Button CandidateC_btn (.out(CandidateC_btn_out));
  Button CandidateD_btn (.out(CandidateD_btn_out));
  and PINMatch_And (PIN_Match, and_2_out, and_3_out);
  Button Admin_Enable_btn (.out(Admin_out));
  and AND_A (VOTEAccepted_A, CandidateA_btn_out, NOR_Q_out);
  and AND_B (VOTEAccepted_B, CandidateB_btn_out, NOR_Q_out);
  and AND_C (VOTEAccepted_C, CandidateC_btn_out, NOR_Q_out);
  and AND_D (VOTEAccepted_D, CandidateD_btn_out, NOR_Q_out);
  and EnableSet_And (EnableSet_And_out, PIN_Match, Admin_out);
  or or_4 (or_4_out, Reset_btn, EnableSet_out);
  LED led_2 (.in(Locked_out));
  Hex_Digit_Display #(.decimalPoint("false")) hex_digit_display_1 (.value(Wrong_count));
  not not_2 (not_2_out, Locked_out);
  Counter #(.max('hf), .width(4)) counter_2 (
    .clr(1'b0), .load(1'b0), .up(1'b1), .count(1'b1), .clk(VOTEAccepted_A), .D(4'b0000), .Q(counter_2_q));  // open: carry
  or OR_1_dup2 (OR_1_out_2, VOTEAccepted_A, VOTEAccepted_B);
  nor NOR_Q (NOR_Q_out, Any_Vote, NOR_Qp_out);
  nor NOR_Qp (NOR_Qp_out, EnableSet_out, NOR_Q_out);
  or OR_2_dup2 (OR_2_out_2, OR_1_out_2, VOTEAccepted_C);
  Counter #(.max('hf), .width(4)) counter_3 (
    .clr(1'b0), .load(1'b0), .up(1'b1), .count(1'b1), .clk(VOTEAccepted_B), .D(4'b0000), .Q(counter_3_q));  // open: carry
  or OR_3_dup2 (Any_Vote, OR_2_out_2, VOTEAccepted_D);
  Counter #(.max('hf), .width(4)) counter_4 (
    .clr(1'b0), .load(1'b0), .up(1'b1), .count(1'b1), .clk(VOTEAccepted_D), .D(4'b0000), .Q(counter_4_q));  // open: carry
  Hex_Digit_Display #(.decimalPoint("false")) hex_digit_display_2 (.value(counter_2_q));
  Counter #(.max('hf), .width(4)) counter_5 (
    .clr(1'b0), .load(1'b0), .up(1'b1), .count(1'b1), .clk(VOTEAccepted_C), .D(4'b0000), .Q(counter_5_q));  // open: carry
  Hex_Digit_Display #(.decimalPoint("false")) hex_digit_display_3 (.value(counter_3_q));
  Adder #(.width(4)) adder_1 (.a(counter_2_q), .b(counter_3_q), .out(adder_1_out), .cin(1'b0));  // open: cout
  Counter #(.max('hf), .width(4)) counter_6 (
    .clr(1'b0), .load(1'b0), .up(1'b1), .count(1'b1), .clk(Any_Vote), .D(4'b0000), .Q(Anyvote_clk));  // open: carry
  Hex_Digit_Display #(.decimalPoint("false")) hex_digit_display_4 (.value(counter_4_q));
  Adder #(.width(4)) adder_2 (.a(adder_1_out), .b(counter_5_q), .out(adder_2_out), .cin(1'b0));  // open: cout
  Hex_Digit_Display #(.decimalPoint("false")) hex_digit_display_5 (.value(counter_5_q));
  Adder #(.width(4)) adder_3 (.a(adder_2_out), .b(counter_4_q), .out(adder_3_out), .cin(1'b0));  // open: cout
  Comparator #(.width(4)) comparator_1 (.a(adder_3_out), .b(Anyvote_clk), .eq(comparator_1_eq));  // open: gt, lt
  Hex_Digit_Display #(.decimalPoint("false")) hex_digit_display_6 (.value(Anyvote_clk));
  Comparator #(.mode("unsigned"), .width(4)) comparator_2 (
    .a(Anyvote_clk), .b(4'b1110), .gt(comparator_2_gt));  // open: eq, lt
  not not_3 (not_3_out, comparator_1_eq);
  LED Tamper (.in(not_3_out));
  LED OverVoting_Alarm_LED (.in(comparator_2_gt));

  // Notes on the sheet:
  //   Abtn
  //   Bbtn
  //   Cbtn
  //   Block 9
  //   Dbtn
  //   Any Press
  //   enabled
  //   PIN_Match
  //   Admin_in
  //   EnableSet_in
  //   vote blocked LED
  //   Block 2
  //   Wrong Press
  //   Block 1
  //   Block 10
  //   A_Btn
  //   A_Enable
  //   B_Btn
  //   B_Enable
  //   C_Btn
  //   C_Enable
  //   D_Btn
  //   D_Enable
  //   Block 4
  //   Not locked
  //   Block 3
  //   Block 5_A
  //   Block 5_B
  //   Block 5_D
  //   Block 5_C
  //   #1
  //   #2
  //   #3
  //   Block 6
endmodule

module main_clean (
  input  pin0,
  input  pin1,
  input  pin2,
  input  pin3,
  output [3:0] A,
  output [3:0] B,
  output [3:0] C,
  output [3:0] D,
  output [3:0] Total_vote
);

  wire Admin_enable_btn_out, block_2_1_admin_out, block_2_1_enableset_and_output, block_2_1_pin_match,
       block_3_1_enabled, block_4_1_any_vote, block_4_1_voteaccepted_a, block_4_1_voteaccepted_b,
       block_4_1_voteaccepted_c, block_4_1_voteaccepted_d, block_7_1_light, block_8_1_light,
       block_9_1_blocked, block_10_1_enableset_out, block_10_1_locked_out, CandidateA_btn_out,
       CandidateB_btn_out, CandidateC_btn_out, CandidateD_btn_out, Lockout_Reset_Btn_out;
  wire [3:0] block_10_1_wrong_count;

  Button Admin_enable_btn (.out(Admin_enable_btn_out));
  LED Vote_blocked_led (.in(block_9_1_blocked));
  block_9 block_9_1 (
    .A_btn(CandidateA_btn_out), .B_btn(CandidateB_btn_out), .C_btn(CandidateC_btn_out),
    .D_btn(CandidateD_btn_out), .Enabled(block_3_1_enabled), .Blocked(block_9_1_blocked));
  block_2 block_2_1 (
    .pin_bit0(pin0), .pin_bit1(pin1), .pin_bit2(pin2), .admin_in(Admin_enable_btn_out), .pin_bit3(pin3),
    .PIN_Match(block_2_1_pin_match), .EnableSet_and_output(block_2_1_enableset_and_output),
    .Admin_out(block_2_1_admin_out));
  Button Lockout_Reset_Btn (.out(Lockout_Reset_Btn_out));
  Button CandidateA_btn (.out(CandidateA_btn_out));
  Button CandidateB_btn (.out(CandidateB_btn_out));
  Button CandidateC_btn (.out(CandidateC_btn_out));
  Button CandidateD_btn (.out(CandidateD_btn_out));
  block_4 block_4_1 (
    .A_Btn(CandidateA_btn_out), .A_Enable(block_3_1_enabled), .B_Btn(CandidateB_btn_out),
    .B_Enable(block_3_1_enabled), .C_Btn(CandidateC_btn_out), .C_Enable(block_3_1_enabled),
    .D_Btn(CandidateD_btn_out), .D_Enable(block_3_1_enabled), .VOTEAccepted_A(block_4_1_voteaccepted_a),
    .VOTEAccepted_B(block_4_1_voteaccepted_b), .VOTEAccepted_C(block_4_1_voteaccepted_c),
    .Any_Vote(block_4_1_any_vote), .VOTEAccepted_D(block_4_1_voteaccepted_d));
  block_3 block_3_1 (.R(block_4_1_any_vote), .S(block_10_1_enableset_out), .Enabled(block_3_1_enabled));
  block_10 block_10_1 (
    .Reset_btn(Lockout_Reset_Btn_out), .PIN_match(block_2_1_pin_match), .Admin_btn(block_2_1_admin_out),
    .EnableSet_in(block_2_1_enableset_and_output), .EnableSet_out(block_10_1_enableset_out),
    .Locked_out(block_10_1_locked_out), .Wrong_count(block_10_1_wrong_count));
  LED Locked_Out_LED (.in(block_10_1_locked_out));
  Hex_Digit_Display hex_digit_display_1 (.value(block_10_1_wrong_count));  // open: dp
  block_5 block_5A (.Counter_clock_pin(block_4_1_voteaccepted_a), .out_put(A));
  block_5 block_5B (.Counter_clock_pin(block_4_1_voteaccepted_b), .out_put(B));
  block_5 block_5C (.Counter_clock_pin(block_4_1_voteaccepted_c), .out_put(C));
  block_5 block_5D (.Counter_clock_pin(block_4_1_voteaccepted_d), .out_put(D));
  block_6 block_6_1 (.in_1(block_4_1_any_vote), .Anyvote_clk(Total_vote));
  block_7 block_7_1 (.oneA(A), .oneB(B), .twoB(C), .threeB(D), .comparator_b(Total_vote), .light(block_7_1_light));
  LED Tamper_check (.in(block_7_1_light));
  LED overvoting_alaram (.in(block_8_1_light));
  block_8 block_8_1 (.A(Total_vote), .light(block_8_1_light));
endmodule

module block_1 (
);

  Button CandidateA_btn ();  // open: out
  Button CandidateB_btn ();  // open: out
  Button CandidateC_btn ();  // open: out
  Button CandidateD_btn ();  // open: out
endmodule

module block_2 (
  input  pin_bit0,
  input  pin_bit1,
  input  pin_bit2,
  input  admin_in,
  input  pin_bit3,
  output PIN_Match,
  output EnableSet_and_output,
  output Admin_out
);

  wire and_1_out, and_2_out, xnor_1_out, xnor_2_out, xnor_3_out, xnor_4_out;

  xnor xnor_1 (xnor_1_out, pin_bit0, 1'b1);
  xnor xnor_2 (xnor_2_out, pin_bit1, 1'b0);
  xnor xnor_3 (xnor_3_out, pin_bit2, 1'b1);
  xnor xnor_4 (xnor_4_out, pin_bit3, 1'b1);
  and and_1 (and_1_out, xnor_1_out, xnor_2_out);
  and and_2 (and_2_out, xnor_3_out, xnor_4_out);
  and PINMatch_And (PIN_Match, and_1_out, and_2_out);
  Button Admin_Enable_btn ();  // open: out
  and EnableSet_And (EnableSet_and_output, PIN_Match, admin_in);

  assign Admin_out = admin_in;
endmodule

module block_3 (
  input  R,
  input  S,
  output Enabled
);

  wire NOR_Qp_out;

  nor NOR_Q (Enabled, R, NOR_Qp_out);
  nor NOR_Qp (NOR_Qp_out, S, Enabled);
endmodule

module block_4 (
  input  A_Btn,
  input  A_Enable,
  input  B_Btn,
  input  B_Enable,
  input  C_Btn,
  input  C_Enable,
  input  D_Btn,
  input  D_Enable,
  output VOTEAccepted_A,
  output VOTEAccepted_B,
  output VOTEAccepted_C,
  output Any_Vote,
  output VOTEAccepted_D
);

  wire or_1_out, or_2_out;

  and AND_A (VOTEAccepted_A, A_Btn, A_Enable);
  and AND_B (VOTEAccepted_B, B_Btn, B_Enable);
  and AND_C (VOTEAccepted_C, C_Btn, C_Enable);
  and AND_D (VOTEAccepted_D, D_Btn, D_Enable);
  or or_1 (or_1_out, VOTEAccepted_A, VOTEAccepted_B);
  or or_2 (or_2_out, or_1_out, VOTEAccepted_C);
  or or_3 (Any_Vote, or_2_out, VOTEAccepted_D);
endmodule

module block_5 (
  input  Counter_clock_pin,
  output [3:0] out_put
);

  Counter #(.max('hf), .width(4)) counter_1 (
    .clr(1'b0), .load(1'b0), .up(1'b1), .count(1'b1), .clk(Counter_clock_pin), .D(4'b0000), .Q(out_put));  // open: carry
  Hex_Digit_Display #(.decimalPoint("false")) hex_digit_display_1 (.value(out_put));
endmodule

module block_6 (
  input  in_1,
  output [3:0] Anyvote_clk
);

  Counter #(.max('hf), .width(4)) counter_1 (
    .clr(1'b0), .load(1'b0), .up(1'b1), .count(1'b1), .clk(in_1), .D(4'b0000), .Q(Anyvote_clk));  // open: carry
  Hex_Digit_Display #(.decimalPoint("false")) hex_digit_display_1 (.value(Anyvote_clk));
endmodule

module block_7 (
  input  [3:0] oneA,
  input  [3:0] oneB,
  input  [3:0] twoB,
  input  [3:0] threeB,
  input  [3:0] comparator_b,
  output light
);

  wire comparator_1_eq;
  wire [3:0] adder_1_out, adder_2_out, adder_3_out;

  Adder #(.width(4)) adder_1 (.a(oneA), .b(oneB), .out(adder_1_out), .cin(1'b0));  // open: cout
  Adder #(.width(4)) adder_2 (.a(adder_1_out), .b(twoB), .out(adder_2_out), .cin(1'b0));  // open: cout
  Adder #(.width(4)) adder_3 (.a(adder_2_out), .b(threeB), .out(adder_3_out), .cin(1'b0));  // open: cout
  Comparator #(.width(4)) comparator_1 (.a(adder_3_out), .b(comparator_b), .eq(comparator_1_eq));  // open: gt, lt
  not not_1 (light, comparator_1_eq);
  LED led_1 (.in(light));

  // Notes on the sheet:
  //   #1
  //   #2
  //   #3
endmodule

module block_8 (
  input  [3:0] A,
  output light
);

  LED OverVoting_Alarm_LED (.in(light));
  Comparator #(.mode("unsigned"), .width(4)) comparator_1 (.a(A), .b(4'b1110), .gt(light));  // open: eq, lt
endmodule

module block_9 (
  input  A_btn,
  input  B_btn,
  input  C_btn,
  input  D_btn,
  input  Enabled,
  output Blocked
);

  wire OR_1_out, OR_2_out, OR_3_out;

  or OR_1 (OR_1_out, A_btn, B_btn);
  or OR_2 (OR_2_out, OR_1_out, C_btn);
  or OR_3 (OR_3_out, OR_2_out, D_btn);
  D_Flip_Flop d_ff_1 (.D(1'b1), .clk(OR_3_out), .Q(Blocked), .preset(1'b0), .reset(Enabled));  // open: Qn
  LED led_1 (.in(Blocked));

  // Notes on the sheet:
  //   Any Press
endmodule

module block_10 (
  input  Reset_btn,
  input  PIN_match,
  input  Admin_btn,
  input  EnableSet_in,
  output EnableSet_out,
  output Locked_out,
  output [3:0] Wrong_count
);

  wire and_2_out, not_1_out, not_2_out, or_1_out;

  not not_1 (not_1_out, PIN_match);
  and and_1 (EnableSet_out, EnableSet_in, not_2_out);
  and and_2 (and_2_out, not_1_out, Admin_btn);
  Counter #(.max('h3), .ongoal("stay"), .width(4)) counter_1 (
    .clr(or_1_out), .load(1'b0), .up(1'b1), .count(1'b1), .clk(and_2_out), .D(4'b0000), .carry(Locked_out),
    .Q(Wrong_count));
  or or_1 (or_1_out, Reset_btn, EnableSet_out);
  LED led_1 (.in(Locked_out));
  not not_2 (not_2_out, Locked_out);
  Hex_Digit_Display #(.decimalPoint("false")) hex_digit_display_1 (.value(Wrong_count));

  // Notes on the sheet:
  //   Wrong Press
  //   Not locked
endmodule
